# Fritzing sketch Lab2 (saved by Fritzing 0.9.3b)

parts:
  Raspberry_Pi_1 = Raspberry Pi 3 [part_number=RPI-3-V1.2]
  U1 = XBee
  U2 = NodeMCU V1.0
  Part1 = Arduino Uno (Rev3) - ICSP
  U3 = XBee
  U4 = XBee
  Part2 = MQ-9 breakout

nets:
  3V3: Raspberry_Pi_1.3v3, U1.VCC
  N1: Raspberry_Pi_1.GPIO15, U1.pin2
  N2: Raspberry_Pi_1.GPIO14, U1.pin3
  GND: Raspberry_Pi_1.GND, U1.GND
  3V3_2: U2.3V3, U4.VCC
  GND_2: U2.GND, U4.GND
  N3: U2.RX, U4.pin2
  N4: U2.TX, U4.pin3
  N5: Part1.A0, Part2.AO
  GND_3: Part1.GND, U3.GND, Part2.GND
  N6: Part1.D0/RX, U3.pin2
  N7: Part1.D1/TX, U3.pin3
  3V3_3: Part1.3V3, U3.VCC
  5V: Part1.5V, Part2.VCC

notes:
  MQ-135
  ESP8266 ESP-12E

custom parts:
  NodeMCU V1.0: ESP8266 based NodeMCU
  MQ-9 breakout: SKU: 101284
